# Fritzing sketch board_sketch (saved by Fritzing 0.9.5d)
breadboards: 1

parts:
  A-Z_Delivery_ESP32_LOLIN32 = Wemos Lolin 32
  R1 = Resistor [tolerance=±5% resistance=220 package=THT]
  R2 = Resistor [tolerance=±5% resistance=220 package=THT]
  R3 = Resistor [tolerance=±5% resistance=220 package=THT]
  R4 = Resistor [tolerance=±5% resistance=220 package=THT]
  LED1 = LED - 5mm [color="Blue (430nm)" package="5 mm [THT]"]
  LED2 = LED - 5mm [color="Green (555nm)" package="5 mm [THT]"]
  LED3 = LED - 5mm [color="Yellow (595nm)" package="5 mm [THT]"]
  LED4 = LED - 5mm [color="Red (633nm)" package="5 mm [THT]"]
  S1 = Pushbutton [package="[SMD]"]
  S2 = Pushbutton [package="[SMD]"]
  Magnetic_Door_Sensor = Reed switch [package=THT]
  PIR_Sensor = HC-SR501 Body Sensor Module
  Speaker = Buzzer 12mm [package=buzzer-ccv]
  BAT1 = LIPO-2000mAh [package=lipo-2000]

nets:
  N1: A-Z_Delivery_ESP32_LOLIN32.pin_0, A-Z_Delivery_ESP32_LOLIN32.pin_25, A-Z_Delivery_ESP32_LOLIN32.pin_34, PIR_Sensor.VCC
  N2: A-Z_Delivery_ESP32_LOLIN32.pin_13, Speaker.1
  N3: A-Z_Delivery_ESP32_LOLIN32.pin_15, A-Z_Delivery_ESP32_LOLIN32.pin_17, A-Z_Delivery_ESP32_LOLIN32.pin_20, A-Z_Delivery_ESP32_LOLIN32.pin_30, A-Z_Delivery_ESP32_LOLIN32.pin_31, A-Z_Delivery_ESP32_LOLIN32.pin_37, LED1.cathode, LED2.cathode, LED3.cathode, LED4.cathode, S1.Pin_1, S1.Pin_2, S2.Pin_1, S2.Pin_2, Magnetic_Door_Sensor.pin_2, PIR_Sensor.GND, Speaker.2, BAT1.-
  N4: A-Z_Delivery_ESP32_LOLIN32.pin_16, BAT1.+
  N5: A-Z_Delivery_ESP32_LOLIN32.pin_18, Magnetic_Door_Sensor.pin_1
  N6: A-Z_Delivery_ESP32_LOLIN32.pin_19, R1.Pin_1
  N7: A-Z_Delivery_ESP32_LOLIN32.pin_22, S1.Pin_3, S1.Pin_4
  N8: A-Z_Delivery_ESP32_LOLIN32.pin_23, S2.Pin_3, S2.Pin_4
  N9: A-Z_Delivery_ESP32_LOLIN32.pin_24, R2.Pin_1
  N10: A-Z_Delivery_ESP32_LOLIN32.pin_26, PIR_Sensor.OUT
  N11: A-Z_Delivery_ESP32_LOLIN32.pin_27, R3.Pin_1
  N12: A-Z_Delivery_ESP32_LOLIN32.pin_29, R4.Pin_1
  N13: R1.Pin_0, LED1.anode
  N14: R2.Pin_0, LED2.anode
  N15: R3.Pin_0, LED3.anode
  N16: R4.Pin_0, LED4.anode

custom parts:
  Wemos Lolin 32: Wemos Lolin 32 wifi and blue tooth board based on the ESP-32 cpu, digital I/Os 26, analog inputs 12, clock 240mhz, Flash 4Mbytes, lipo battery charger (500ma connection broken out on breadboard but not pcb), usb. The mounting holes are only set on the silkscreen, if you want actual holes in the pcb copy the hole from the pcb menu in parts over the top of the hole in the silkscreen.
  HC-SR501 Body Sensor Module: Pyroelectric Infrared PIR Motion Sensor Detector Module
